# Fritzing sketch Auto plant watering (saved by Fritzing 0.9.3b)
circuit board: 5cm x 6cm
perfboards: 1

parts:
  RHT1 = Humidity and Temperature Sensor RHT03
  M1 = DC Motor
  D1 = Rectifier Diode [part_number=1N4001 package="300 mil [THT]"]
  Power_plug1 = Power plug
  R1 = Resistor [tolerance=±5% resistance=1k package=THT]
  Q2 = Basic FET N-Channel [package="TO220 [THT]"]
  Q1 = NPN-Transistor [package="TO92 [THT]"]
  Часть1 = Arduino Uno (Rev3)
  R2 = Rotary Potentiometer (Small) [maximum_resistance=100kΩ package=THT]

nets:
  VCC: RHT1.Vcc, Часть1.5V, R2.leg2
  N1: RHT1.Data-signal, Q1.C
  N2: RHT1.GND_2, Часть1.A0
  VCC_2: M1.pin_1, D1.cathode, Power_plug1.VCC, Часть1.VIN
  N3: M1.pin_2, D1.anode, Q2.drain
  GND: Power_plug1.GND, Q2.source, Q1.E, Часть1.GND, R2.leg1
  N4: R1.Pin_0, Часть1.D4
  N5: R1.Pin_1, Q1.B
  N6: Q2.gate, Часть1.D6_PWM
  N7: Часть1.A1, R2.wiper

// code stored in the sketch: auto Plant Watering.ino
//#define MOTOR_PIN   13 //????????? ?? ?????
#define MOTOR_PIN   6 //PWM 
#define MEASURE_PIN   A0
#define MEASURE_POWER_PIN   4
#define POT_PIN_LOW     A1
//#define POT_PIN_HIGH    A1

bool humidyflag = false;
int  meas_del=10; //???????? ????? ????????? ?????????? (???????)
int  hum_del=5;  //????? ?????? (???????)

void setup()
{
  Serial.begin(9600);
  pinMode(MOTOR_PIN, OUTPUT);
  pinMode(MEASURE_PIN, INPUT);
  pinMode(MEASURE_POWER_PIN, OUTPUT);
  pinMode(POT_PIN_LOW, INPUT);
 // pinMode(POT_PIN_LOW, INPUT);
}

int moist_measure ()
{
  digitalWrite(MEASURE_POWER_PIN, HIGH);
  delay(1000);
  int moist1 = 1024 - analogRead(MEASURE_PIN);
  digitalWrite(MEASURE_POWER_PIN, LOW);
  return moist1;
}

void loop()
{
int moist_lim_high = 500; 
//analogRead (POT_PIN_HIGH);  
//int moist_lim_low  = 200; 
int moist_lim_low = analogRead(POT_PIN_LOW);
int moist = moist_measure();

    if (moist < moist_lim_low)  humidyflag = true;
    if (moist > moist_lim_high) humidyflag = false;
    //bool humidy = (moist > moist_lim_low && moist < moist_lim_high && humidyflag) || (humidyflag);

    if (humidyflag) {
    analogWrite (MOTOR_PIN, 90); 
    delay (1000*hum_del); //???????? ??????
    analogWrite (MOTOR_PIN, LOW); 
    }
   delay (1000*meas_del); // ???????? ????? ????????? ??????????
   Serial.print(moist_lim_low);
	 Serial.print(moist);
   Serial.print("\t");
   Serial.println(humidyflag);
  }
