# Fritzing sketch Auto plant watering_2 (saved by Fritzing 0.9.3b)
circuit board: 5.5cm x 5.5cm
perfboards: 1

parts:
  RHT1 = Humidity and Temperature Sensor RHT03
  M1 = DC Motor  # not connected
  R1 = Resistor [tolerance=±5% resistance=1k package=THT]
  Q2 = Basic FET N-Channel [package="TO220 [THT]"]
  Q1 = NPN-Transistor [package="TO92 [THT]"]
  Power_plug1 = Power plug
  Часть1 = Arduino Uno (Rev3)
  LED1 = LED - 5mm [color="Red (633nm)" package="5 mm [THT]"]
  R3 = Resistor [tolerance=±5% resistance=220 package=THT]
  S1 = Pushbutton [package="[THT]"]
  D1 = Rectifier Diode [part_number=1N4001 package="300 mil [THT]"]

nets:
  VCC: RHT1.Vcc, Часть1.5V
  N1: RHT1.Data-signal, Q1.C
  N2: RHT1.GND_2, Часть1.A0
  N3: R1.Pin_0, Часть1.D8
  N4: R1.Pin_1, Q1.B
  N5: Q2.gate, Часть1.D10_PWM/SS
  N6: Q2.drain, D1.cathode
  GND: Q2.source, Q1.E, Power_plug1.GND, Часть1.GND, R3.Pin_0, S1.Pin_3, S1.Pin_4
  VCC_2: Power_plug1.VCC, Часть1.VIN, D1.anode
  N7: Часть1.D2, S1.Pin_1, S1.Pin_2
  N8: Часть1.D4, LED1.cathode
  N9: LED1.anode, R3.Pin_1

custom parts:
  Power plug: power plug

// code stored in the sketch: auto Plant Watering.ino
#define LED_PIN   13 //????????? ?? ?????
#define MOTOR_PIN   6 //PWM 
#define MEASURE_PIN   A0
#define MEASURE_POWER_PIN   4
#define POT_PIN_LOW     A1
//#define POT_PIN_HIGH    A1

bool humidyflag = false;
int  meas_del=6; //(?? 30*10)
int  hum_del=5;  //????? ?????? (???????)

void setup()
{
  Serial.begin(9600);
  pinMode(MOTOR_PIN, OUTPUT);
  pinMode(MEASURE_PIN, INPUT);
  pinMode(MEASURE_POWER_PIN, OUTPUT);
  pinMode(POT_PIN_LOW, INPUT);
  pinMode(LED_PIN, OUTPUT);
 // pinMode(POT_PIN_LOW, INPUT);
}

int moist_measure ()
{
  digitalWrite(MEASURE_POWER_PIN, HIGH);
  delay(1000);
  int moist1 = 1024 - analogRead(MEASURE_PIN);
  digitalWrite(MEASURE_POWER_PIN, LOW);
  return moist1;
}

int moisture ()
{
  analogWrite (MOTOR_PIN, 100); 
  digitalWrite (LED_PIN, HIGH);
  delay (1000*hum_del); //???????? ??????
  analogWrite (MOTOR_PIN, LOW); 
  digitalWrite (LED_PIN, LOW);;
  return;
}

void loop()
{
int moist_lim_high = 700; 
//analogRead (POT_PIN_HIGH);  
int moist_lim_low  = 200; 
int moist_lim_low_2 = analogRead(POT_PIN_LOW);
int moist = moist_measure();

    if (moist < moist_lim_low)  humidyflag = true;
    if (moist > moist_lim_high) humidyflag = false;
    //bool humidy = (moist > moist_lim_low && moist < moist_lim_high && humidyflag) || (humidyflag);

   Serial.print(moist_lim_low);
   Serial.print("\t");
   Serial.print(moist_lim_low_2);
   Serial.print("\t");
   Serial.print(moist);
   Serial.print("\t");
   Serial.println(humidyflag);
   
   if ((millis() mod meas_del)=0 || (humidyflag)) moisture;
  }
